# Fritzing sketch APA102-2020_strip (saved by Fritzing 0.9.3b)
circuit board: 1.4cm x 0.3cm
breadboards: 1

parts:
  RGB_SMD_LED1 = APA102-2020 [package=2020]
  RGB_SMD_LED2 = APA102-2020 [package=2020]
  Pad1 = Pad [width=1.5 height=1.1000000000000001 connect=center]
  Pad2 = Pad [width=1.5 height=1.1000000000000001 connect=center]
  Pad3 = Pad [width=1.5 height=1.1000000000000001 connect=center]
  Pad4 = Pad [width=1.5 height=1.1000000000000001 connect=center]
  Pad6 = Pad [width=1.5 height=1.1000000000000001 connect=center]
  Pad5 = Pad [width=1.5 height=1.1000000000000001 connect=center]
  Pad7 = Pad [width=1.5 height=1.1000000000000001 connect=center]
  Pad8 = Pad [width=1.5 height=1.1000000000000001 connect=center]

nets:
  VCC: RGB_SMD_LED1.VCC, RGB_SMD_LED2.VCC, Pad6.pad, Pad7.pad
  N1: RGB_SMD_LED1.CKO, Pad1.pad
  N2: RGB_SMD_LED1.SDO, Pad2.pad
  N3: RGB_SMD_LED1.SDI, RGB_SMD_LED2.SDO
  N4: RGB_SMD_LED1.CKI, RGB_SMD_LED2.CKO
  GND: RGB_SMD_LED1.GND, RGB_SMD_LED2.GND, Pad5.pad, Pad8.pad
  N5: RGB_SMD_LED2.SDI, Pad4.pad
  N6: RGB_SMD_LED2.CKI, Pad3.pad

notes:
  CO
  DO
  DI
  CI
  V+
  V-

custom parts:
  APA102-2020: APA102-2020 2mm x 2mm Individually addressable LED. Note: there are at least 3 and possibly more incompatible footprints for these LEDs from different manufacturers. This particular part is for the APA Electronic Co APA-102-2020 device (data sheet at http://neon-world.com/uploads/wenjian/20apa.pdf). Check the PCB foot print of the device you have before using this part.
