# Fritzing sketch Schematics_Rhizome_21-10 (saved by Fritzing 1.0.5)
breadboards: 1

parts:
  Part1 = ESP-WROOM-32 [ESP-32S] Module [part_number=ESP-WROOM-32]
  A1 = Haptic Bzzz
  U1 = 74AHCT125 [part_number=SN74AHCT125 package=dil14]  # not connected
  C1 = Capacitor Polarized [package=cpol-radial-1000uf-63v]  # not connected
  Part2 = ws2812b [package="smd 2812b"]  # not connected
  IC1 = Stereo 3.7W Class D Amplifier [mn="Maxim Integrated" mpn=MAX98357BETE+ package=16-TQFN]  # not connected
  Part3 = PN532 Elechouse RFID NFC Module V3
  IC2 = Stereo 3.7W Class D Amplifier [mn="Maxim Integrated" mpn=MAX98357BETE+ package=16-TQFN]  # not connected
  A2 = Haptic Bzzz
  A3 = Haptic Bzzz
  A4 = Haptic Bzzz
  Part4 = ws2812b [package="smd 2812b"]  # not connected
  Part5 = ws2812b [package="smd 2812b"]  # not connected
  Part6 = ws2812b [package="smd 2812b"]  # not connected
  Part7 = ws2812b [package="smd 2812b"]  # not connected
  Part8 = ws2812b [package="smd 2812b"]  # not connected
  Part9 = ws2812b [package="smd 2812b"]  # not connected
  Part10 = ws2812b [package="smd 2812b"]  # not connected
  Part11 = PN532 Elechouse RFID NFC Module V3
  SPKR1 = Loudspeaker  # not connected
  SPKR2 = Loudspeaker  # not connected
  VCC1 = 4 x AAA Battery Mount [internal_resistance=0.1Ω]  # not connected

nets:
  N1: Part1.IO18, A1.TRIG, A2.TRIG, A3.TRIG, A4.TRIG
  N2: Part1.IO19, A1.SCL, A2.SCL, A3.SCL, A4.SCL
  N3: Part1.IO20, A1.SDA, A2.SDA, A3.SDA, A4.SDA
  N4: Part1.IO21, Part11.SDA
  N5: Part1.RXD0, Part11.SCL
  N6: Part1.TXD0, Part3.SCL
  N7: Part1.IO22, Part3.SDA
  N8: A1.2-5V, A2.2-5V, A3.2-5V, A4.2-5V
  GND: A1.GND, A2.GND, A3.GND, A4.GND
  GND_2: Part3.GND, Part11.GND
  VCC: Part3.VCC, Part11.VCC

custom parts:
  ESP-WROOM-32 [ESP-32S] Module: Espressif ESP-WROOM-32 WiFi/Bluetooth LE microcontroller module also known as the Ai-Thinker ESP-32S module with similar formfactor. The ESP32 is a microcontroller chip with WiFi and BLE capabilities. The chip is developed by Espressif and is the successor to the popular ESP8266 WiFi module.
  Haptic Bzzz: This DRV2605L haptic driver breakout with linear actuator will really get you buzzing! The powerful haptic buzz (bzzz!) is programmable with a range of built-in patterns, or you can program your own. Check out our full range of Breakout's and Breakout Garden's here This little haptic driver and actuator is great for adding some buzzy feedback to your projects. We combined it with our Trackball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
  74AHCT125: Quad Level-Shifter (3V to 5V) Quadruple Bus Buffer Gates With 3-State Outputs
  Stereo 3.7W Class D Amplifier: Mono 3.2W Class D Amplifier Datasheet: https://datasheets.maximintegrated.com/en/ds/MAX98357A-MAX98357B.pdf The MAX98357B is an easy-to-use, low-cost, digital pulse-code modulation (PCM) input Class D amplifier that provides industry-leading Class AB audio performance with Class D efficiency. The digital audio interface automatically recognizes up to 35 different PCM and TDM clocking schemes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
  PN532 Elechouse RFID NFC Module V3: NFC is a popular technology in recent years. We often heard this work while smart phone company such as Samsung or HTC introduces their latest high-end phones. Almost all the high-end phone in the market support NFC. Near field communication (NFC) is a set of standards for smart phones and similar devices to establish radio communication with each other by touching them together or bringing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
