# Fritzing sketch 2020footprintforshare (saved by Fritzing 0.9.3b)
circuit board: 2cm x 3.5cm
breadboards: 1

parts:
  RGB_SMD_LED63 = SMD RGB LED (WS2812) [package=5050]
  RGB_SMD_LED8 = SMD RGB LED (WS2812) [package=5050]
  RGB_SMD_LED14 = SMD RGB LED (WS2812) [package=5050]
  RGB_SMD_LED13 = SMD RGB LED (WS2812) [package=5050]
  Q3 = MOSFET-NCHANNEL [package=sot23-3]
  RGB_SMD_LED52 = SMD RGB LED (WS2812) [package=5050]
  RGB_SMD_LED54 = SMD RGB LED (WS2812) [package=5050]
  RGB_SMD_LED56 = SMD RGB LED (WS2812) [package=5050]
  RGB_SMD_LED57 = SMD RGB LED (WS2812) [package=5050]
  V++ = Pad [width=2.5 height=10 connect=center]
  Data = Pad [width=1.5 height=10 connect=center]
  Clk = Pad [width=1.5 height=10 connect=center]
  GND = Pad [width=2.5 height=10 connect=center]
  Pad45 = Pad [width=0.5 height=1 connect=center]  # not connected
  Pad47 = Pad [width=0.80000000000000004 height=0.5 connect=center]  # not connected
  Pad50 = Pad [width=0.80000000000000004 height=0.29999999999999999 connect=center]  # not connected
  Pad51 = Pad [width=0.80000000000000004 height=0.5 connect=center]  # not connected
  Pad54 = Pad [width=0.80000000000000004 height=0.5 connect=center]  # not connected
  Pad55 = Pad [width=0.80000000000000004 height=0.5 connect=center]  # not connected
  Pad57 = Pad [width=0.80000000000000004 height=0.29999999999999999 connect=center]  # not connected
  Pad58 = Pad [width=0.5 height=1 connect=center]  # not connected
  RGB_SMD_LED59 = SMD RGB LED (WS2812) [package=5050]
  RGB_SMD_LED60 = SMD RGB LED (WS2812) [package=5050]
  RGB_SMD_LED61 = SMD RGB LED (WS2812) [package=5050]
  RGB_SMD_LED62 = SMD RGB LED (WS2812) [package=5050]
  V++_2 = Pad [width=2.5 height=10 connect=center]
  Data_2 = Pad [width=1.5 height=10 connect=center]
  Clk_2 = Pad [width=1.5 height=10 connect=center]
  GND_2 = Pad [width=2.5 height=10 connect=center]
  Pad65 = Pad [width=0.80000000000000004 height=0.29999999999999999 connect=center]  # not connected
  Pad66 = Pad [width=0.80000000000000004 height=0.5 connect=center]  # not connected
  Pad60 = Pad [width=0.80000000000000004 height=0.5 connect=center]  # not connected
  Pad63 = Pad [width=0.5 height=1 connect=center]  # not connected
  Pad62 = Pad [width=0.80000000000000004 height=0.5 connect=center]  # not connected
  Pad64 = Pad [width=0.5 height=1 connect=center]  # not connected
  Pad61 = Pad [width=0.80000000000000004 height=0.5 connect=center]  # not connected
  Pad59 = Pad [width=0.80000000000000004 height=0.29999999999999999 connect=center]  # not connected
  control = Pad [width=2.5 height=10 connect=center]
  Pad69 = Pad [width=0.80000000000000004 height=0.5 connect=center]
  Pad70 = Pad [width=0.5 height=1 connect=center]
  Pad72 = Pad [width=0.5 height=1 connect=center]
  Pad73 = Pad [width=0.80000000000000004 height=0.5 connect=center]  # not connected
  Pad74 = Pad [width=0.80000000000000004 height=0.29999999999999999 connect=center]
  V++_3 = Pad [width=2.5 height=10 connect=center]
  Data_3 = Pad [width=1.5 height=10 connect=center]
  Clk_3 = Pad [width=1.5 height=10 connect=center]
  GND_3 = Pad [width=2.5 height=10 connect=center]
  controll = Pad [width=2.5 height=10 connect=center]
  Pad68 = Pad [width=0.80000000000000004 height=0.5 connect=center]
  Pad71 = Pad [width=0.80000000000000004 height=0.5 connect=center]  # not connected
  Pad67 = Pad [width=0.80000000000000004 height=0.29999999999999999 connect=center]
  Pad75 = Pad [width=0.80000000000000004 height=0.29999999999999999 connect=center]
  Pad76 = Pad [width=0.80000000000000004 height=0.5 connect=center]
  Pad77 = Pad [width=0.80000000000000004 height=0.5 connect=center]
  Pad78 = Pad [width=0.5 height=1 connect=center]
  Pad79 = Pad [width=0.80000000000000004 height=0.5 connect=center]  # not connected
  Pad80 = Pad [width=0.5 height=1 connect=center]
  Pad81 = Pad [width=0.80000000000000004 height=0.5 connect=center]  # not connected
  Pad82 = Pad [width=0.80000000000000004 height=0.29999999999999999 connect=center]
  Pad83 = Pad [width=0.80000000000000004 height=0.29999999999999999 connect=center]
  Pad84 = Pad [width=0.80000000000000004 height=0.29999999999999999 connect=center]  # not connected
  Pad85 = Pad [width=0.80000000000000004 height=0.5 connect=center]  # not connected
  Pad86 = Pad [width=0.80000000000000004 height=0.5 connect=center]
  Pad87 = Pad [width=0.80000000000000004 height=0.5 connect=center]
  Pad88 = Pad [width=0.80000000000000004 height=0.5 connect=center]
  Pad89 = Pad [width=0.5 height=1 connect=center]
  Pad90 = Pad [width=0.5 height=1 connect=center]
  Pad91 = Pad [width=0.80000000000000004 height=0.5 connect=center]  # not connected
  Pad92 = Pad [width=0.80000000000000004 height=0.5 connect=center]  # not connected
  Pad93 = Pad [width=0.5 height=1 connect=center]
  Pad94 = Pad [width=0.5 height=1 connect=center]
  Pad95 = Pad [width=0.80000000000000004 height=0.5 connect=center]  # not connected
  Pad96 = Pad [width=0.80000000000000004 height=0.5 connect=center]  # not connected
  Pad97 = Pad [width=0.80000000000000004 height=0.29999999999999999 connect=center]
  Pad98 = Pad [width=0.80000000000000004 height=0.29999999999999999 connect=center]
  Q4 = MOSFET-NCHANNEL [package=sot23-3]
  Pad99 = Pad [width=5.1838004255037307 height=2.8982010809160799 connect=center]
  Pad100 = Pad [width=2.9526727655801315 height=3.1110239281877954 connect=center]
  Pad101 = Pad [width=2.6444272842762793 height=2.8027784468839751 connect=center]
  Pad102 = Pad [width=3.2231275062320486 height=3.0162782222222222 connect=center]
  Pad103 = Pad [width=2.6066365436243446 height=2.5025357533824684 connect=center]
  Pad104 = Pad [width=3.6705712346863204 height=2.9041881728987158 connect=center]
  Pad105 = Pad [width=4.5588579252153831 height=3.7868919254818523 connect=center]
  Pad106 = Pad [width=3.2231275062320486 height=3.0162782222222222 connect=center]

nets:
  N1: RGB_SMD_LED63.DOut, V++.pad
  N2: RGB_SMD_LED63.DIn, RGB_SMD_LED8.VDD
  N3: RGB_SMD_LED63.VCC, RGB_SMD_LED8.NC
  N4: RGB_SMD_LED63.NC, Data.pad
  N5: RGB_SMD_LED63.VDD, Clk.pad
  N6: RGB_SMD_LED63.VSS, GND.pad
  N7: RGB_SMD_LED8.DIn, RGB_SMD_LED13.VDD
  N8: RGB_SMD_LED8.VCC, RGB_SMD_LED13.NC
  N9: RGB_SMD_LED14.NC, RGB_SMD_LED13.VCC
  N10: RGB_SMD_LED14.VDD, RGB_SMD_LED13.DIn
  N11: Q3.G, control.pad
  N12: Q3.S, GND_2.pad, Pad101.pad, Pad104.pad
  VSS: Q3.D, RGB_SMD_LED59.VSS, RGB_SMD_LED60.VSS, RGB_SMD_LED61.VSS, RGB_SMD_LED62.VSS, Pad99.pad, Pad100.pad
  N13: RGB_SMD_LED52.VDD, RGB_SMD_LED54.DIn
  N14: RGB_SMD_LED52.VSS, RGB_SMD_LED54.DOut
  N15: RGB_SMD_LED54.VDD, RGB_SMD_LED56.DIn
  N16: RGB_SMD_LED54.VSS, RGB_SMD_LED56.DOut
  N17: RGB_SMD_LED56.VDD, RGB_SMD_LED57.DIn
  N18: RGB_SMD_LED56.VSS, RGB_SMD_LED57.DOut
  N19: RGB_SMD_LED59.DOut, RGB_SMD_LED60.DOut, RGB_SMD_LED61.DOut, RGB_SMD_LED62.DOut, V++_2.pad
  N20: RGB_SMD_LED59.DIn, RGB_SMD_LED60.VDD
  N21: RGB_SMD_LED59.VCC, RGB_SMD_LED60.NC
  N22: RGB_SMD_LED59.NC, Data_2.pad
  N23: RGB_SMD_LED59.VDD, Clk_2.pad
  N24: RGB_SMD_LED60.DIn, RGB_SMD_LED62.VDD
  N25: RGB_SMD_LED60.VCC, RGB_SMD_LED62.NC
  N26: RGB_SMD_LED61.NC, RGB_SMD_LED62.VCC
  N27: RGB_SMD_LED61.VDD, RGB_SMD_LED62.DIn
  N28: Pad69.pad, Data_3.pad
  N29: Pad70.pad, Pad78.pad, Pad89.pad, Pad90.pad, Q4.D, Pad105.pad, Pad106.pad
  N30: Pad72.pad, V++_3.pad, Pad80.pad, Pad93.pad, Pad94.pad
  N31: Pad74.pad, Clk_3.pad
  N32: GND_3.pad, Q4.S, Pad102.pad, Pad103.pad
  N33: controll.pad, Q4.G
  N34: Pad68.pad, Pad77.pad
  N35: Pad67.pad, Pad82.pad
  N36: Pad75.pad, Pad98.pad
  N37: Pad76.pad, Pad87.pad
  N38: Pad83.pad, Pad97.pad
  N39: Pad86.pad, Pad88.pad

notes:
  1
  3
  4
  2
  23
  24
