# Fritzing sketch Rhizome_V2_AvecSpeaker (saved by Fritzing 1.0.5)
circuit board: 10.4418cm x 8.4715cm
breadboards: 3

parts:
  A1 = Teensy 4.0
  AMP1 = PAM8403 6W Stereo Amplifier
  C1 = Electrolytic Capacitor [capacitance=1000μF voltage=10V package="1010 [SMD, electrolytic]"]
  R1 = Resistor [tolerance=±5% power=0.25W resistance=330 package=THT]
  J3 = female pin header, 3 pins [form="♀ (female)"]
  U3 = 74AHCT125 [part_number=SN74AHCT125 package=dil14]
  R2 = Resistor [tolerance=±5% power=0.25W resistance=330 package=THT]
  R3 = Resistor [tolerance=±5% power=0.25W resistance=330 package=THT]
  R4 = Resistor [tolerance=±5% power=0.25W resistance=330 package=THT]
  J4 = female pin header, 4 pins [form="♀ (female)"]
  J5 = female pin header, 4 pins [form="♀ (female)"]
  J8 = female pin header, 3 pins [form="♀ (female)"]
  J9 = female pin header, 3 pins [form="♀ (female)"]
  C4 = Electrolytic Capacitor [capacitance=1000μF voltage=10V package="1010 [SMD, electrolytic]"]
  J10 = female pin header, 4 pins [form="♀ (female)"]
  J2 = female pin header, 5 pins [form="♀ (female)"]
  J1 = female pin header, 5 pins [form="♀ (female)"]
  J7 = female pin header, 2 pins [form="♀ (female)"]
  J6 = female pin header, 2 pins [form="♀ (female)"]
  J11 = female pin header, 2 pins [form="♀ (female)"]

nets (from the pcb view):
  N1: A1.pin_1, A1.pin_17, A1.pin_32, AMP1.POWER-, C1.+, U3.1OE, U3.2OE, U3.GND, J4.pin2, J5.pin2, J8.pin3, J9.pin3, C4.-, J10.pin4, J2.pin1, J2.pin3, J1.pin3, J1.pin5, J11.pin1
  N2: A1.pin_2, R4.Pin_0
  N3: A1.pin_3, R3.Pin_0
  N4: A1.pin_8, J1.pin1
  N5: A1.pin_9, J1.pin4
  N6: A1.pin_10, J1.pin2
  N7: A1.pin_14, U3.2A
  N8: A1.pin_16, A1.pin_31, J4.pin1, J5.pin1, J8.pin1, J9.pin1
  N9: A1.pin_20, U3.1A
  N10: A1.pin_21, J2.pin4
  N11: A1.pin_22, J2.pin2
  N12: A1.pin_23, J5.pin4
  N13: A1.pin_24, J5.pin3
  N14: A1.pin_25, J4.pin4
  N15: A1.pin_26, J4.pin3
  N16: A1.pin_27, J2.pin5
  N17: A1.pin33, AMP1.POWER+, C1.-, U3.VCC, C4.+, J10.pin1, J11.pin2
  N18: AMP1.ROUT-, J7.pin1
  N19: AMP1.ROUT+, J7.pin2
  N20: AMP1.LOUT+, J6.pin2
  N21: AMP1.LOUT-, J6.pin1
  N22: AMP1.INPUTL, J3.pin1
  N23: AMP1.INPUTG, J3.pin2
  N24: AMP1.INPUTR, J3.pin3
  N25: R1.Pin_0, J10.pin2
  N26: R1.Pin_1, U3.1Y
  N27: U3.2Y, R2.Pin_0
  N28: R2.Pin_1, J10.pin3
  N29: R3.Pin_1, J9.pin2
  N30: R4.Pin_1, J8.pin2

notes:
  +
  -
  APA-102
  SERIAL-1
  SERIAL-2
  INDIVIDUAL_LED - 1
  INDIVIDUAL_LED - 2
  SPEAKER - 1
  SPEAKER - 2
  SHIELD
  AMPLI
  HAPTIC - 1
  HAPTIC - 2
  SDA
  SCL
  DO
  CO
  R
  L
  Pwr
  LED_STRIP
  LED_1
  LED_2
  HAPTICS_1
  HAPTICS_2
  RX
  TX
  F
  SERIAL_1
  SERIAL_2
  VERSION 1.0
  PCB DESIGN:
  Justin Lepitre
  MERCI À
  Gabriel Pelland
  Matthieu Gagnon Lamarre
  Clément Boucher

custom parts:
  Teensy 4.0: The Teensy is a complete USB-based microcontoller development system, in a very small footprint, capable of implementing many types of projects. All programming is done via the USB port. No special programmer is needed, only a standard micro-USB cable and a PC or Macintosh with a USB port. (Oct 2023 added the VBUS pad at user request.)
  PAM8403 6W Stereo Amplifier: PAM8403 6 Watt Stereo Amplifier
  74AHCT125: Quad Level-Shifter (3V to 5V) Quadruple Bus Buffer Gates With 3-State Outputs
