# Fritzing sketch SYNAPSE_RHIZOME_PCB_V1 (saved by Fritzing 1.0.5)
circuit board: 11.7042cm x 7.14766cm
breadboards: 3

parts:
  A1 = Teensy 4.0
  R1 = Resistor [tolerance=±5% power=0.25W resistance=330 package=THT]
  U3 = 74AHCT125 [part_number=SN74AHCT125 package=dil14]
  R2 = Resistor [tolerance=±5% power=0.25W resistance=330 package=THT]
  J4 = female pin header, 4 pins [form="♀ (female)"]
  J5 = female pin header, 4 pins [form="♀ (female)"]
  J8 = female pin header, 3 pins [form="♀ (female)"]
  J9 = female pin header, 3 pins [form="♀ (female)"]
  J10 = female pin header, 4 pins [form="♀ (female)"]
  J2 = female pin header, 5 pins [form="♀ (female)"]
  J1 = female pin header, 5 pins [form="♀ (female)"]
  J11 = female pin header, 2 pins [form="♀ (female)"]
  R5 = Resistor [tolerance=±5% power=0.25W resistance=330 package=THT]
  R6 = Resistor [tolerance=±5% power=0.25W resistance=330 package=THT]
  C8 = Electrolytic Capacitor [capacitance=1000μF voltage=10V package="300 mil [THT, electrolytic]"]
  C6 = Electrolytic Capacitor [capacitance=1000μF voltage=10V package="200 mil [THT, electrolytic]"]
  C7 = Electrolytic Capacitor [capacitance=1000μF voltage=10V package="200 mil [THT, electrolytic]"]
  C2 = Electrolytic Capacitor [capacitance=100μF voltage=6.3V package="200 mil [THT, electrolytic]"]
  C4 = Electrolytic Capacitor [capacitance=100μF voltage=10V package="200 mil [THT, electrolytic]"]

nets (from the pcb view):
  N1: A1.pin_1, A1.pin_17, A1.pin_32, U3.1OE, U3.2OE, U3.GND, U3.3OE, U3.4OE, J4.pin2, J5.pin2, J8.pin3, J9.pin3, J10.pin1, J2.pin1, J2.pin3, J1.pin3, J1.pin5, J11.pin1, C8.-, C6.-, C7.-, C2.-, C4.-
  N2: A1.pin_2, U3.4A
  N3: A1.pin_3, U3.3A
  N4: A1.pin_8, J1.pin1
  N5: A1.pin_9, J1.pin4
  N6: A1.pin_10, J1.pin2
  N7: A1.pin_14, U3.2A
  N8: A1.pin_20, U3.1A
  N9: A1.pin_21, J2.pin4
  N10: A1.pin_22, J2.pin2
  N11: A1.pin_23, J5.pin4
  N12: A1.pin_24, J5.pin3
  N13: A1.pin_25, J4.pin3
  N14: A1.pin_26, J4.pin4
  N15: A1.pin_27, J2.pin5
  N16: A1.pin_31, J4.pin1, J5.pin1, C2.+, C4.+
  N17: A1.pin33, U3.VCC, J8.pin1, J9.pin1, J10.pin4, J11.pin2, C8.+, C6.+, C7.+
  N18: R1.Pin_0, U3.1Y
  N19: R1.Pin_1, J10.pin2
  N20: U3.2Y, R2.Pin_0
  N21: U3.3Y, R6.Pin_1
  N22: U3.4Y, R5.Pin_1
  N23: R2.Pin_1, J10.pin3
  N24: J8.pin2, R6.Pin_0
  N25: J9.pin2, R5.Pin_0

notes:
  APA-102
  SERIAL-1
  SERIAL-2
  INDIVIDUAL_LED - 1
  INDIVIDUAL_LED - 2
  SPEAKER - 1
  SPEAKER - 2
  SHIELD
  AMPLI
  HAPTIC - 1
  HAPTIC - 2
  +
  -
  SDA
  SCL
  DI
  CI
  Pwr
  LED_STRIP
  LED_1
  LED_2
  HAPTICS_1
  HAPTICS_2
  RX
  TX
  F
  SERIAL_2
  SERIAL_3
  VERSION 1.0
  PCB DESIGN:
  Justin Lepitre
  MERCI À
  Gabriel Pelland
  Matthieu Gagnon Lamarre
  Clément Boucher
  SYNAPSE

custom parts:
  Teensy 4.0: The Teensy is a complete USB-based microcontoller development system, in a very small footprint, capable of implementing many types of projects. All programming is done via the USB port. No special programmer is needed, only a standard micro-USB cable and a PC or Macintosh with a USB port. (Oct 2023 added the VBUS pad at user request.)
  74AHCT125: Quad Level-Shifter (3V to 5V) Quadruple Bus Buffer Gates With 3-State Outputs
